# Fritzing sketch clock (saved by Fritzing 0.9.4)
circuit board: 8.46667cm x 5.64444cm
breadboards: 2

parts:
  Part1 = Arduino Nano (Rev3.0)
  U1 = 555 Timer [package="DIP8 [THT]"]
  R1 = Resistor [tolerance=±5% resistance=1k package=THT]
  R3 = Resistor [tolerance=±5% resistance=220 package=THT]
  LED1 = smd LED [color="Yellow (595nm)" package="1206 [SMD]"]
  C1 = Electrolytic Capacitor [capacitance=1µF package="100 mil [THT, electrolytic]"]
  C2 = Tantalum Capacitor [capacitance=10µF package="B 3528 [SMD, tantalum]"]
  C3 = Tantalum Capacitor [capacitance=0.1mF package="B 3528 [SMD, tantalum]"]
  R4 = Rotary Potentiometer (Large) [maximum_resistance=100kΩ package=THT]
  R5 = Resistor [tolerance=±5% resistance=1k package=THT]
  S1 = Pushbutton [package="[SMD]"]
  U2 = 555 Timer [package="DIP8 [THT]"]
  LED2 = smd LED [color="Yellow (595nm)" package="1206 [SMD]"]
  R6 = Resistor [tolerance=±5% resistance=220 package=THT]
  R7 = Resistor [tolerance=±5% resistance=1M package=THT]
  C4 = Tantalum Capacitor [capacitance=0.1mF package="B 3528 [SMD, tantalum]"]
  C5 = Tantalum Capacitor [capacitance=10µF package="B 3528 [SMD, tantalum]"]
  R8 = Resistor [tolerance=±5% resistance=1k package=THT]

nets:
  N1: Part1.GND, U1.Ground, R3.Pin_0, C2.-, C3.-, S1.Pin_3, S1.Pin_4, U2.Ground, R6.Pin_0, C4.-, C5.-
  N2: Part1.5V, U1.Reset, U1.Vcc_Supply_Voltage, R1.Pin_0, C3.+, U2.Reset, U2.Vcc_Supply_Voltage, R7.Pin_0, R8.Pin_0
  N3: U1.Trigger, U1.Threshold, C1.+, R4.wiper
  N4: U1.Output, LED1.anode
  N5: U1.Control_Voltage, C2.+
  N6: U1.Discharge, R1.Pin_1, R5.Pin_1
  N7: R3.Pin_1, LED1.cathode
  N8: R4.leg2, R5.Pin_0
  N9: S1.Pin_1, S1.Pin_2, U2.Trigger, R8.Pin_1
  N10: U2.Output, LED2.anode
  N11: U2.Control_Voltage, C5.+
  N12: U2.Threshold, U2.Discharge, R7.Pin_1, C4.+
  N13: LED2.cathode, R6.Pin_1
